// Logisim project CPU.circ as structural Verilog
module log8 (
  output [7:0] out_1
);

  wire alu_1_eaccmx, alu_1_ealu, alu_1_salu, and_1_out, button_1_out, clock_1_out;
  wire [3:0] alu_1_flg_out, counter_1_q, pull_resistor_1_node, rom_1_data_3;
  wire [4:0] rom_1_data_2;
  wire [7:0] ACC_q, alu_1_alu_out, log8_regfile_1_o8, multiplexer_1_out, register_2_q, register_3_q;
  wire [15:0] log8_prg_1_probe, log8_regfile_1_o16, log8_regfile_1_pbab, log8_regfile_1_pbcd,
       log8_regfile_1_pbef, log8_regfile_1_phg, log8_stp_1_probe, register_4_q;
  wire [31:0] rom_1_data;

  Register register_1 (.D(log8_regfile_1_o8), .en(rom_1_data_3[0]), .Q(out_1), .clk(clock_1_out));  // open: clr
  and and_1 (and_1_out, rom_1_data_3[3], clock_1_out);
  Counter #(.max('hf), .width(4)) counter_1 (
    .Q(counter_1_q), .clk(clock_1_out), .clr(and_1_out));  // open: load, D, count, carry, up
  Register register_2 (.D(log8_regfile_1_o8), .en(rom_1_data_3[2]), .Q(register_2_q), .clk(clock_1_out));  // open: clr
  Clock clock_1 (.out(clock_1_out));
  Register register_3 (.D(log8_regfile_1_o8), .en(rom_1_data_3[1]), .Q(register_3_q), .clk(clock_1_out));  // open: clr
  Pull_Resistor pull_resistor_1 (.node(pull_resistor_1_node));
  ROM #(.addrWidth(16), .dataWidth(32)) rom_1 (
    .addr({pull_resistor_1_node, register_2_q, counter_1_q}),
    .data({rom_1_data[31:27], rom_1_data_3, rom_1_data_2, rom_1_data[17:0]}));
  log8_regfile log8_regfile_1 (
    .in_4(register_3_q), .i8(log8_regfile_1_o8), .Clk(clock_1_out), .RFileCtrl(rom_1_data_2),
    .PbCD(log8_regfile_1_pbcd), .PbEF(log8_regfile_1_pbef), .PHG(log8_regfile_1_phg),
    .PbAB(log8_regfile_1_pbab), .o16(log8_regfile_1_o16), .o8(log8_regfile_1_o8));
  // Probe on log8_regfile_1_pbab
  // Probe on log8_regfile_1_pbcd
  // Probe on log8_regfile_1_pbef
  // Probe on log8_regfile_1_phg
  // Probe on log8_regfile_1_o16
  // Probe on log8_regfile_1_o8
  // Probe on log8_stp_1_probe
  log8_stp log8_stp_1 (
    .clk(clock_1_out), .i8(log8_regfile_1_o8), .ctrl(rom_1_data[17:15]), .probe(log8_stp_1_probe),
    .o8(log8_regfile_1_o8), .o16(log8_regfile_1_o16));
  // Probe on log8_prg_1_probe
  log8_prg log8_prg_1 (
    .clk(clock_1_out), .i8(log8_regfile_1_o8), .ctrl(rom_1_data[14:11]), .probe(log8_prg_1_probe),
    .o8(log8_regfile_1_o8), .o16(log8_regfile_1_o16));
  // Probe on rom_1_data[31:27]
  Register #(.width(16)) register_4 (
    .D(log8_regfile_1_o16), .en(rom_1_data[8]), .Q(register_4_q), .clk(clock_1_out));  // open: clr
  // Probe on log8_regfile_1_o8
  // Probe on alu_1_alu_out
  // Probe on alu_1_flg_out
  Button button_1 (.out(button_1_out));
  RAM #(.addrWidth(16), .clearpin("true"), .databus("bidir"), .enables("line")) ram_1 (
    .addr(register_4_q), .data(log8_regfile_1_o8), .clr(button_1_out));  // open: we, oe, clk
  Multiplexer #(.width(8)) multiplexer_1 (
    .in0(log8_regfile_1_o8), .in1(alu_1_alu_out), .out(multiplexer_1_out), .sel(alu_1_eaccmx));
  Register ACC (.D(multiplexer_1_out), .en(alu_1_salu), .Q(ACC_q), .clk(clock_1_out));  // open: clr
  // Probe on ACC_q
  assign log8_regfile_1_o8 = alu_1_ealu ? ACC_q : 8'bz;  // Controlled_Buffer controlled_buffer_1
  ALU alu_1 (
    .A_IN(log8_regfile_1_o8), .B_IN(ACC_q), .ALUCTRL(rom_1_data[7:0]), .FLG_OUT(alu_1_flg_out),
    .ALU_OUT(alu_1_alu_out), .eALU(alu_1_ealu), .eACCMx(alu_1_eaccmx), .sALU(alu_1_salu));

  // Notes on the sheet:
  //   contents of rom_1 (hex, n*v repeats v):
  //   4900 2000200 4900 800200 4000000 11*0 4900 2000200 4900 800200 4000000 11*0 4900 2000200 4900 800200
  //   4000000 11*0 4900 2000200 4900 800200 4000000 11*0 4900 2000200 4900 800200 4000000 11*0 4900
  //   2000200 4900 800200 4000000 11*0 4900 2000200 4900 800200 4000000 11*0 4900 2000200 4900 800200
  //   4000000 11*0 4900 2000200 4900 800200 4000000 11*0 4900 2000200 4900 800200 4000000 11*0 4900
  //   2000200 4900 800200 4000000 11*0 4900 2000200 4900 800200 4000000 11*0 4900 2000200 4900 800200
  //   4000000 11*0 4900 2000200 4900 800200 4000000 11*0 4900 2000200 4900 800200 4000000 11*0 4900
  //   2000200 4900 800200 4000000 11*0 4900 2000200 4900 800200 4900 40200 4000000 57*0 4900 2000200 4900
  //   800200 4900 140200 4900 540200 4000000
endmodule

module log8_prg (
  input  [7:0] i8,
  input  clk,
  input  [3:0] ctrl,
  output [15:0] probe,
  output [15:0] o16,
  output [7:0] o8
);

  wire and_1_out, counter_1_carry, not_1_out, not_2_out;

  not not_1 (not_1_out, ctrl[3]);
  not not_2 (not_2_out, ctrl[2]);
  and and_1 (and_1_out, ctrl[2], not_1_out);
  Counter counter_1 (
    .load(and_1_out), .D(i8), .count(ctrl[3]), .Q(probe[7:0]), .carry(counter_1_carry), .up(not_2_out),
    .clk(clk));  // open: clr
  assign o16 = ctrl[0] ? probe : 16'bz;  // Controlled_Buffer controlled_buffer_1
  assign o8 = ctrl[1] ? probe[15:8] : 8'bz;  // Controlled_Buffer controlled_buffer_2
  Counter counter_2 (
    .load(and_1_out), .D(probe[7:0]), .count(counter_1_carry), .Q(probe[15:8]), .up(not_2_out), .clk(clk));  // open: carry, clr
endmodule

module log8_stp (
  input  [7:0] i8,
  input  clk,
  input  [2:0] ctrl,
  output [15:0] probe,
  output [15:0] o16,
  output [7:0] o8
);

  Register register_1 (.D(i8), .en(ctrl[2]), .Q(probe[7:0]), .clk(clk));  // open: clr
  assign o16 = ctrl[0] ? probe : 16'bz;  // Controlled_Buffer controlled_buffer_1
  assign o8 = ctrl[1] ? probe[15:8] : 8'bz;  // Controlled_Buffer controlled_buffer_2
  Register register_2 (.D(probe[7:0]), .en(ctrl[2]), .Q(probe[15:8]), .clk(clk));  // open: clr
endmodule

module log8_regfile (
  input  Clk,
  input  [7:0] i8,
  input  [4:0] RFileCtrl,
  input  [7:0] in_4,
  output [7:0] o8,
  output [15:0] PbAB,
  output [15:0] o16,
  output [15:0] PbCD,
  output [15:0] PbEF,
  output [15:0] PHG
);

  wire not_1_out, or_1_out, or_2_out, or_3_out, or_4_out;
  wire [2:0] demultiplexer_2_out0, demultiplexer_2_out1, demultiplexer_2_out2, demultiplexer_2_out3,
       demultiplexer_2_out4, demultiplexer_2_out5, demultiplexer_2_out6, demultiplexer_2_out7,
       multiplexer_1_out, multiplexer_2_out_2;
  wire [2:1] demultiplexer_1_out0;
  wire [7:0] multiplexer_2_out;

  Demultiplexer demultiplexer_1 (
    .out0(demultiplexer_1_out0[1]), .out1(demultiplexer_1_out0[2]), .in(RFileCtrl[1]), .sel(RFileCtrl[2]));
  Demultiplexer #(.select(3), .width(3)) demultiplexer_2 (
    .out0(demultiplexer_2_out0), .out1(demultiplexer_2_out1), .out2(demultiplexer_2_out2),
    .out3(demultiplexer_2_out3), .out4(demultiplexer_2_out4), .out5(demultiplexer_2_out5),
    .out6(demultiplexer_2_out6), .out7(demultiplexer_2_out7), .in({demultiplexer_1_out0, RFileCtrl[0]}),
    .sel(multiplexer_1_out));
  Multiplexer #(.width(3)) multiplexer_1 (
    .in0(multiplexer_2_out_2), .in1(multiplexer_2_out[2:0]), .out(multiplexer_1_out), .sel(not_1_out));
  not not_1 (not_1_out, RFileCtrl[3]);
  Multiplexer #(.width(8)) multiplexer_2 (
    .in0(in_4), .in1({in_4[7:5], RFileCtrl[4], in_4[3:1], RFileCtrl[4]}),
    .out({multiplexer_2_out[7], multiplexer_2_out_2, multiplexer_2_out[3:0]}), .sel(RFileCtrl[2]));
  assign o8 = demultiplexer_2_out0[1] ? PbAB[7:0] : 8'bz;  // Controlled_Buffer controlled_buffer_1
  Register register_1 (.D(i8), .en(demultiplexer_2_out0[0]), .Q(PbAB[7:0]), .clk(Clk));  // open: clr
  assign o8 = demultiplexer_2_out2[1] ? PbCD[7:0] : 8'bz;  // Controlled_Buffer controlled_buffer_2
  Register register_2 (.D(i8), .en(demultiplexer_2_out2[0]), .Q(PbCD[7:0]), .clk(Clk));  // open: clr
  assign o8 = demultiplexer_2_out4[1] ? PbEF[7:0] : 8'bz;  // Controlled_Buffer controlled_buffer_3
  Register register_3 (.D(i8), .en(demultiplexer_2_out4[0]), .Q(PbEF[7:0]), .clk(Clk));  // open: clr
  assign o8 = demultiplexer_2_out6[1] ? PHG[7:0] : 8'bz;  // Controlled_Buffer controlled_buffer_4
  Register register_4 (.D(i8), .en(demultiplexer_2_out6[0]), .Q(PHG[7:0]), .clk(Clk));  // open: clr
  Register register_5 (.D(i8), .en(demultiplexer_2_out1[0]), .Q(PbAB[15:8]), .clk(Clk));  // open: clr
  Register register_6 (.D(i8), .en(demultiplexer_2_out3[0]), .Q(PbCD[15:8]), .clk(Clk));  // open: clr
  Register register_7 (.D(i8), .en(demultiplexer_2_out5[0]), .Q(PbEF[15:8]), .clk(Clk));  // open: clr
  Register register_8 (.D(i8), .en(demultiplexer_2_out7[0]), .Q(PHG[15:8]), .clk(Clk));  // open: clr
  assign o16 = or_1_out ? PbAB : 16'bz;  // Controlled_Buffer controlled_buffer_5
  assign o8 = demultiplexer_2_out1[1] ? PbAB[15:8] : 8'bz;  // Controlled_Buffer controlled_buffer_6
  or or_1 (or_1_out, demultiplexer_2_out0[2], demultiplexer_2_out1[2]);
  assign o16 = or_2_out ? PbCD : 16'bz;  // Controlled_Buffer controlled_buffer_7
  assign o8 = demultiplexer_2_out3[1] ? PbCD[15:8] : 8'bz;  // Controlled_Buffer controlled_buffer_8
  or or_2 (or_2_out, demultiplexer_2_out2[2], demultiplexer_2_out3[2]);
  assign o16 = or_3_out ? PbEF : 16'bz;  // Controlled_Buffer controlled_buffer_9
  assign o8 = demultiplexer_2_out5[1] ? PbEF[15:8] : 8'bz;  // Controlled_Buffer controlled_buffer_10
  or or_3 (or_3_out, demultiplexer_2_out4[2], demultiplexer_2_out5[2]);
  assign o16 = or_4_out ? PHG : 16'bz;  // Controlled_Buffer controlled_buffer_11
  assign o8 = demultiplexer_2_out7[1] ? PHG[15:8] : 8'bz;  // Controlled_Buffer controlled_buffer_12
  or or_4 (or_4_out, demultiplexer_2_out6[2], demultiplexer_2_out7[2]);
endmodule

module ALU (
  input  [7:0] ALUCTRL,
  input  [7:0] A_IN,
  input  [7:0] B_IN,
  output sALU,
  output eALU,
  output eACCMx,
  output [7:0] ALU_OUT,
  output [3:0] FLG_OUT
);

  wire [3:3] pull_resistor_1_node;
  wire [7:0] adder_1_out, and_1_out, demultiplexer_1_out0, demultiplexer_1_out1, demultiplexer_1_out2,
       demultiplexer_1_out3, demultiplexer_1_out4, demultiplexer_1_out5, demultiplexer_1_out6,
       demultiplexer_1_out7, demultiplexer_2_out0, demultiplexer_2_out1, demultiplexer_2_out2,
       demultiplexer_2_out3, demultiplexer_2_out4, demultiplexer_2_out5, demultiplexer_2_out6,
       demultiplexer_2_out7, not_1_out, or_1_out, shifter_1_out, shifter_2_out, xor_1_out;

  Demultiplexer #(.select(3), .width(8)) demultiplexer_1 (
    .out0(demultiplexer_1_out0), .out1(demultiplexer_1_out1), .out2(demultiplexer_1_out2),
    .out3(demultiplexer_1_out3), .out4(demultiplexer_1_out4), .out5(demultiplexer_1_out5),
    .out6(demultiplexer_1_out6), .out7(demultiplexer_1_out7), .in(A_IN), .sel(ALUCTRL[7:5]));
  Demultiplexer #(.select(3), .width(8)) demultiplexer_2 (
    .out0(demultiplexer_2_out0), .out1(demultiplexer_2_out1), .out2(demultiplexer_2_out2),
    .out3(demultiplexer_2_out3), .out4(demultiplexer_2_out4), .out5(demultiplexer_2_out5),
    .out6(demultiplexer_2_out6), .out7(demultiplexer_2_out7), .in(B_IN), .sel(ALUCTRL[7:5]));
  Adder adder_1 (
    .a(demultiplexer_1_out0), .b(demultiplexer_2_out0), .out(adder_1_out), .cin(ALUCTRL[3]), .cout(FLG_OUT[3]));
  Shifter shifter_1 (.in(demultiplexer_1_out1), .\dist (demultiplexer_2_out1[2:0]), .out(shifter_1_out));
  Shifter #(.shift("lr")) shifter_2 (
    .in(demultiplexer_1_out2), .\dist (demultiplexer_2_out2[2:0]), .out(shifter_2_out));
  assign not_1_out = ~demultiplexer_2_out3;  // NOT_Gate not_1, 8 bits wide
  assign and_1_out = demultiplexer_1_out4 & demultiplexer_2_out4;  // AND_Gate and_1, 8 bits wide
  assign or_1_out = demultiplexer_1_out5 | demultiplexer_2_out5;  // OR_Gate or_1, 8 bits wide
  assign xor_1_out = demultiplexer_1_out6 ^ demultiplexer_2_out6;  // XOR_Gate xor_1, 8 bits wide
  Comparator #(.mode("unsigned")) comparator_1 (
    .a(demultiplexer_1_out7), .b(demultiplexer_2_out7), .gt(FLG_OUT[1]), .eq(FLG_OUT[2]));  // open: lt
  or or_2 (FLG_OUT[0], demultiplexer_1_out7[0], demultiplexer_1_out7[1], demultiplexer_1_out7[2], demultiplexer_1_out7[3], demultiplexer_1_out7[4], demultiplexer_1_out7[5], demultiplexer_1_out7[6], demultiplexer_1_out7[7]);
  Pull_Resistor pull_resistor_1 (.node(pull_resistor_1_node[3]));
  Multiplexer #(.enable("true"), .select(3), .width(8)) multiplexer_1 (
    .in0(adder_1_out), .in1(shifter_1_out), .in2(shifter_2_out), .in3(not_1_out), .in4(and_1_out),
    .in5(or_1_out), .in6(xor_1_out), .out(ALU_OUT), .en(ALUCTRL[2]));  // open: in7, sel

  assign eACCMx = ALUCTRL[2];
  assign eALU = ALUCTRL[1];
  assign sALU = ALUCTRL[0];
endmodule
