// Logisim project CPU2.circ as structural Verilog: 9 circuits, main circuit mboard
module mboard (
  input  in_1,
  input  in_2
);

  wire and_1_out, and_2_out, and_3_out, and_4_out, clock_1_out, log8_1_oe, log8_1_we;
  wire [7:0] log8_1_out8, ram_1_data, rom_1_data;
  wire [15:0] log8_1_out16;

  Clock clock_1 (.out(clock_1_out));
  LOG8 log8_1 (
    .HLT(in_2), .Clk(clock_1_out), .Int(in_1), .IN8(log8_1_out8), .WE(log8_1_we), .OE(log8_1_oe),
    .OUT16(log8_1_out16), .OUT8(log8_1_out8));
  // Probe on log8_1_out16
  // Probe on log8_1_out8
  Pull_Resistor pull_resistor_1 (.node(log8_1_out16));
  and and_1 (and_1_out, ~log8_1_out16[14], ~log8_1_out16[15]);  // AND_Gate
  and and_2 (and_2_out, and_1_out, log8_1_oe, ~log8_1_we);  // AND_Gate
  and and_3 (and_3_out, and_1_out, ~log8_1_oe, log8_1_we);  // AND_Gate
  assign log8_1_out8 = and_2_out ? ram_1_data : 8'bz;  // Controlled_Buffer controlled_buffer_1
  RAM #(.addrWidth(14), .databus("bidir"), .enables("line")) ram_1 (
    .addr(log8_1_out16[13:0]), .data(ram_1_data));  // open: we, oe, clk
  assign ram_1_data = and_3_out ? log8_1_out8 : 8'bz;  // Controlled_Buffer controlled_buffer_2
  ROM #(.addrWidth(14)) rom_1 (.addr(log8_1_out16[13:0]), .data(rom_1_data));
  and and_4 (and_4_out, log8_1_out16[14], log8_1_out16[15], log8_1_we);
  assign log8_1_out8 = and_4_out ? rom_1_data : 8'bz;  // Controlled_Buffer controlled_buffer_3

  // Notes on the sheet:
  //   contents of rom_1 (hex, n*v repeats v):
  //   16381*0 f0 0 80
endmodule

module cpu (
  input  CLK,
  input  [7:0] DIN,
  input  INT,
  output [7:0] DOUT,
  output WE,
  output OE,
  output [15:0] ADDR
);

  wire [1:0] CTRL_a, CTRL_b, CTRL_c, CTRL_d;
  wire [2:0] CTRL_mm, CTRL_pc, CTRL_sp;
  wire [3:0] alu_1_z;
  wire [5:0] CTRL_alu;
  wire [7:0] CTRL_inr, multiplexer_2_out, register_1_q, register_2_q, register_3_q, register_4_q;
  wire [15:0] MM_out_7, PC_out_5, SP_out_5;

  // Probe on CTRL_inr
  // Probe on multiplexer_2_out
  Multiplexer #(.disabled("Z"), .width(8)) multiplexer_1 (.in1(multiplexer_2_out), .out(DOUT), .sel(WE));  // open: in0
  Multiplexer #(.disabled("Z"), .width(8)) multiplexer_2 (.in1(DIN), .out(multiplexer_2_out), .sel(OE));  // open: in0
  CTRL_CIRC CTRL (
    .Clk(CLK), .DATABUS(multiplexer_2_out), .FLAG(alu_1_z), .INT(INT), .out_5(ADDR), .MM(CTRL_mm),
    .PC(CTRL_pc), .SP(CTRL_sp), .D(CTRL_d), .C(CTRL_c), .B(CTRL_b), .A(CTRL_a), .ADR({OE, WE}),
    .ALU(CTRL_alu), .INR(CTRL_inr));
  PC_CIRC PC (.in_1(ADDR), .in_3(CTRL_pc), .in_2(CLK), .out_4(ADDR), .out_5(PC_out_5));
  // Probe on PC_out_5
  SP_CIRC SP (.in_1(ADDR), .in_3(CTRL_sp), .in_2(CLK), .out_4(ADDR), .out_5(SP_out_5));
  // Probe on SP_out_5
  MM_CIRC MM (
    .in_4(CTRL_mm), .in_1(ADDR), .in_2(multiplexer_2_out), .in_3(CLK), .out_5(multiplexer_2_out),
    .out_6(ADDR), .out_7(MM_out_7));
  // Probe on MM_out_7
  assign multiplexer_2_out = CTRL_a[0] ? register_1_q : 8'bz;  // Controlled_Buffer controlled_buffer_1
  Register register_1 (.D(multiplexer_2_out), .en(CTRL_a[1]), .Q(register_1_q), .clk(CLK));  // open: clr
  // Probe on ADDR
  assign multiplexer_2_out = CTRL_b[0] ? register_2_q : 8'bz;  // Controlled_Buffer controlled_buffer_2
  Register register_2 (.D(multiplexer_2_out), .en(CTRL_b[1]), .Q(register_2_q), .clk(CLK));  // open: clr
  ALU alu_1 (
    .A(register_1_q), .B(register_2_q), .cin(CTRL_alu[5]), .op3(CTRL_alu[4]), .op2(CTRL_alu[3]),
    .op1(CTRL_alu[2]), .op0(CTRL_alu[1]), .X(CTRL_alu[0]), .O(multiplexer_2_out), .Z(alu_1_z[0]),
    .G(alu_1_z[1]), .E(alu_1_z[2]), .C(alu_1_z[3]));
  assign multiplexer_2_out = CTRL_c[0] ? register_3_q : 8'bz;  // Controlled_Buffer controlled_buffer_3
  Register register_3 (.D(multiplexer_2_out), .en(CTRL_c[1]), .Q(register_3_q), .clk(CLK));  // open: clr
  assign multiplexer_2_out = CTRL_d[0] ? register_4_q : 8'bz;  // Controlled_Buffer controlled_buffer_4
  Register register_4 (.D(multiplexer_2_out), .en(CTRL_d[1]), .Q(register_4_q), .clk(CLK));  // open: clr
endmodule

module ALU (
  input  [7:0] A,
  input  [7:0] B,
  input  cin,
  input  op3,
  input  op2,
  input  op1,
  input  op0,
  input  X,
  output [7:0] O,
  output Z,
  output G,
  output E,
  output C
);

  wire adder_1_cout, subtractor_1_bout;
  wire [7:0] adder_1_out, and_1_out, demultiplexer_1_out0, demultiplexer_1_out1, demultiplexer_1_out2,
       demultiplexer_1_out3, demultiplexer_1_out4, demultiplexer_1_out5, demultiplexer_1_out6,
       demultiplexer_1_out7, demultiplexer_2_out0, demultiplexer_2_out1, demultiplexer_2_out2,
       demultiplexer_2_out3, demultiplexer_2_out4, demultiplexer_2_out6, demultiplexer_2_out7, not_1_out,
       or_1_out, shifter_1_out, shifter_2_out, subtractor_1_out, xor_1_out;

  Demultiplexer #(.select(3), .width(8)) demultiplexer_1 (
    .out0(demultiplexer_1_out0), .out1(demultiplexer_1_out1), .out2(demultiplexer_1_out2),
    .out3(demultiplexer_1_out3), .out4(demultiplexer_1_out4), .out5(demultiplexer_1_out5),
    .out6(demultiplexer_1_out6), .out7(demultiplexer_1_out7), .in(A), .sel({op2, op1, op0}));
  Demultiplexer #(.select(3), .width(8)) demultiplexer_2 (
    .out0(demultiplexer_2_out0), .out1(demultiplexer_2_out1), .out2(demultiplexer_2_out2),
    .out3(demultiplexer_2_out3), .out4(demultiplexer_2_out4), .out6(demultiplexer_2_out6),
    .out7(demultiplexer_2_out7), .in(B), .sel({op2, op1, op0}));  // open: out5
  Adder adder_1 (.a(demultiplexer_1_out0), .b(demultiplexer_2_out0), .out(adder_1_out), .cin(cin), .cout(adder_1_cout));
  Subtractor subtractor_1 (
    .a(demultiplexer_1_out1), .b(demultiplexer_2_out1), .out(subtractor_1_out), .bin(cin),
    .bout(subtractor_1_bout));
  assign and_1_out = demultiplexer_1_out2 & demultiplexer_2_out2;  // AND_Gate and_1, 8 bits wide
  assign or_1_out = demultiplexer_1_out3 | demultiplexer_2_out3;  // OR_Gate or_1, 8 bits wide
  assign xor_1_out = demultiplexer_1_out4 ^ demultiplexer_2_out4;  // XOR_Gate xor_1, 8 bits wide
  assign not_1_out = ~demultiplexer_1_out5;  // NOT_Gate not_1, 8 bits wide
  Shifter #(.shift("rl")) shifter_1 (
    .in(demultiplexer_1_out6), .\dist (demultiplexer_2_out6[2:0]), .out(shifter_1_out));
  Shifter #(.shift("rr")) shifter_2 (
    .in(demultiplexer_1_out7), .\dist (demultiplexer_2_out7[2:0]), .out(shifter_2_out));
  Multiplexer #(.disabled("Z"), .enable("true"), .select(3), .width(8)) multiplexer_1 (
    .in0(adder_1_out), .in1(subtractor_1_out), .in2(and_1_out), .in3(or_1_out), .in4(xor_1_out),
    .in5(not_1_out), .in6(shifter_1_out), .in7(shifter_2_out), .out(O), .sel({op2, op1, op0}), .en(X));
  nor nor_1 (Z, A[0], A[1], A[2], A[3], A[4], A[5], A[6], A[7]);
  Comparator comparator_1 (.a(A), .b(B), .gt(G), .eq(E));  // open: lt
  or or_2 (C, adder_1_cout, subtractor_1_bout);

  // Notes on the sheet:
  //   A: pull=down
  //   B: pull=down
endmodule

module CTRL_CIRC (
  input  INT,
  input  Clk,
  input  [7:0] DATABUS,
  input  [3:0] FLAG,
  output [15:0] out_5,
  output [2:0] MM,
  output [2:0] PC,
  output [2:0] SP,
  output [1:0] D,
  output [1:0] C,
  output [1:0] B,
  output [1:0] A,
  output [1:0] ADR,
  output [5:0] ALU,
  output [7:0] INR
);

  wire and_1_out, d_ff_1_q, j_k_ff_1_q, j_k_ff_1_qn, or_1_out;
  wire [2:0] controlled_buffer_1_out_2, counter_1_q, counter_2_q, CTRL;
  wire [3:0] and_2_out, decoder_1_out0, register_2_q;
  wire [11:11] or_2_out;
  wire [15:0] INTROM_data;
  wire [15:12] controlled_buffer_1_out;
  wire [31:0] INSTROM_data, pull_resistor_3_node;
  wire [31:22] multiplexer_1_out;

  and and_1 (and_1_out, INT, CTRL[2]);
  or or_1 (or_1_out, CTRL[2], controlled_buffer_1_out[15]);
  Register register_1 (.D(DATABUS), .en(CTRL[1]), .Q(INR), .clk(Clk));  // open: clr
  Register #(.width(4)) register_2 (.D(FLAG), .en(CTRL[0]), .Q(register_2_q), .clk(Clk));  // open: clr
  J_K_Flip_Flop #(.trigger("falling")) j_k_ff_1 (
    .J(controlled_buffer_1_out[15]), .clk(Clk), .K(and_1_out), .Q(j_k_ff_1_q), .Qn(j_k_ff_1_qn));  // open: preset, reset
  D_Flip_Flop #(.trigger("falling")) d_ff_1 (
    .clk(Clk), .D(or_1_out), .Q(d_ff_1_q), .reset(d_ff_1_q));  // open: Qn, preset
  Decoder #(.enable("false"), .select(2)) decoder_1 (
    .out0(decoder_1_out0[0]), .out1(decoder_1_out0[1]), .out2(decoder_1_out0[2]), .out3(decoder_1_out0[3]),
    .sel(INR[1:0]));
  Counter #(.max('h7), .trigger("falling"), .width(3)) counter_1 (
    .count(j_k_ff_1_qn), .Q(counter_1_q), .clk(Clk), .clr(d_ff_1_q));  // open: load, D, carry, up
  Counter #(.max('h7), .trigger("falling"), .width(3)) counter_2 (
    .count(j_k_ff_1_q), .Q(counter_2_q), .clk(Clk), .clr(d_ff_1_q));  // open: load, D, carry, up
  assign and_2_out = decoder_1_out0 & register_2_q;  // AND_Gate and_2, 4 bits wide
  or or_2 (or_2_out[11], and_2_out[0], and_2_out[1], and_2_out[2], and_2_out[3]);
  ROM #(.addrWidth(4), .dataWidth(16)) INTROM (.addr({INT, counter_1_q}), .data(INTROM_data));
  ROM #(.addrWidth(12), .dataWidth(32)) INSTROM (.addr({or_2_out[11], INR, counter_2_q}), .data(INSTROM_data));
  assign {controlled_buffer_1_out[15], pull_resistor_3_node[7:6], controlled_buffer_1_out[12], controlled_buffer_1_out_2, pull_resistor_3_node[26:24], pull_resistor_3_node[21:16]} = j_k_ff_1_qn ? INTROM_data : 16'bz;  // Controlled_Buffer controlled_buffer_1
  Pull_Resistor pull_resistor_1 (.node(INSTROM_data));
  Pull_Resistor pull_resistor_2 (.node({controlled_buffer_1_out[15], pull_resistor_3_node[7:6], controlled_buffer_1_out[12], controlled_buffer_1_out_2, pull_resistor_3_node[26:24], pull_resistor_3_node[21:16]}));
  Pull_Resistor pull_resistor_3 (.node(pull_resistor_3_node));
  Multiplexer #(.width(32)) multiplexer_1 (
    .in0(pull_resistor_3_node), .in1(INSTROM_data),
    .out({multiplexer_1_out[31:30], CTRL, MM, multiplexer_1_out[23:22], PC, SP, D, C, B, A, ADR, ALU}),
    .sel(j_k_ff_1_q));
  assign out_5 = controlled_buffer_1_out[12] ? {{13{1'b1}}, controlled_buffer_1_out_2} : 16'bz;  // Controlled_Buffer controlled_buffer_2

  // Notes on the sheet:
  //   Clk: pull=down
  //   contents of INTROM (hex, n*v repeats v):
  //   d010 f011 9010 b010
  //   contents of INSTROM (hex, n*v repeats v):
  //   aa00000 4000000 6*0 aa00000 7*0 aa00000 7*0 aa00000 7*0 aa00000 7*0 aa00000 7*0 aa00000 7*0 aa00000
  //   7*0 aa00000 4000000 6*0 aa00000 7*0 aa00000 7*0 aa00000 7*0 aa00000 7*0 aa00000 7*0 aa00000 7*0
  //   aa00000 7*0 aa00000 2a00100 4000000 5*0 aa00000 2a00200 4000000 5*0 aa00000 7*0 aa00000 7*0 aa00000
  //   7*0 aa00000 7*0 aa00000 7*0 aa00000 7*0 aa00000 7*0 aa00000 7*0 aa00000 7*0 aa00000 7*0 aa00000 7*0
  //   aa00000 7*0 aa00000 7*0 aa00000 7*0 aa00000 7*0 aa00000 7*0 aa00000 7*0 aa00000 7*0 aa00000 7*0
  //   aa00000 7*0 aa00000 7*0 aa00000 7*0 aa00000 7*0 aa00000 7*0 aa00000 7*0 aa00000 7*0 aa00000 7*0
  //   aa00000 7*0 aa00000 7*0 aa00000 7*0 aa00000 7*0 aa00000 7*0 aa00000 7*0 aa00000 7*0 aa00000 7*0
  //   aa00000 7*0 aa00000 7*0 aa00000 7*0 aa00000 7*0 aa00000 7*0 aa00000 7*0 aa00000 7*0 aa00000 7*0
  //   aa00000 7*0 aa00000 7*0 aa00000 7*0 aa00000 7*0 aa00000 7*0 aa00000 7*0 aa00000 7*0 aa00000 7*0
  //   aa00000 7*0 aa00000 7*0 aa00000 7*0 aa00000 7*0 aa00000 7*0 aa00000 7*0 aa00000 7*0 aa00000 7*0
  //   aa00000 7*0 aa00000 7*0 aa00000 7*0 aa00000 7*0 aa00000 7*0 aa00000 7*0 aa00000 7*0 aa00000 7*0
  //   aa00000 7*0 aa00000 7*0 aa00000 7*0 aa00000 7*0 aa00000 7*0 aa00000 7*0 aa00000 7*0 aa00000 7*0
  //   aa00000 7*0 aa00000 7*0 aa00000 7*0 aa00000 7*0 aa00000 7*0 aa00000 7*0 aa00000 7*0 aa00000 7*0
  //   aa00000 7*0 aa00000 7*0 aa00000 7*0 aa00000 7*0 aa00000 7*0 aa00000 7*0 aa00000 7*0 aa00000 7*0
  //   aa00000 7*0 aa00000 7*0 aa00000 7*0 aa00000 7*0 aa00000 7*0 aa00000 7*0 aa00000 7*0 aa00000 7*0
  //   aa00000 7*0 aa00000 7*0 aa00000 7*0 aa00000 7*0 aa00000 7*0 aa00000 7*0 aa00000 7*0 aa00000 7*0
  //   aa00000 7*0 aa00000 7*0 aa00000 7*0 aa00000 7*0 aa00000 7*0 aa00000 7*0 aa00000 7*0 aa00000 7*0
  //   aa00000 7*0 aa00000 7*0 aa00000 7*0 aa00000 7*0 aa00000 7*0 aa00000 7*0 aa00000 7*0 aa00000 7*0
  //   aa00000 7*0 aa00000 7*0 aa00000 7*0 aa00000 7*0 aa00000 7*0 aa00000 7*0 aa00000 7*0 aa00000 7*0
  //   aa00000 7*0 aa00000 7*0 aa00000 7*0 aa00000 7*0 aa00000 7*0 aa00000 7*0 aa00000 7*0 aa00000 7*0
  //   aa00000 7*0 aa00000 7*0 aa00000 7*0 aa00000 7*0 aa00000 7*0 aa00000 7*0 aa00000 7*0 aa00000 7*0
  //   aa00000 7*0 aa00000 7*0 aa00000 7*0 aa00000 7*0 aa00000 7*0 aa00000 7*0 aa00000 7*0 aa00000 7*0
  //   aa00000 7*0 aa00000 7*0 aa00000 7*0 aa00000 7*0 aa00000 7*0 aa00000 7*0 aa00000 7*0 aa00000 7*0
  //   aa00000 7*0 aa00000 7*0 aa00000 7*0 aa00000 7*0 aa00000 7*0 aa00000 7*0 aa00000 7*0 aa00000 7*0
  //   aa00000 7*0 aa00000 7*0 aa00000 7*0 aa00000 7*0 aa00000 7*0 aa00000 7*0 aa00000 7*0 aa00000 7*0
  //   aa00000 7*0 aa00000 7*0 aa00000 7*0 aa00000 7*0 aa00000 7*0 aa00000 7*0 aa00000 7*0 aa00000 7*0
  //   aa00000 7*0 aa00000 7*0 aa00000 7*0 aa00000 7*0 aa00000 7*0 aa00000 7*0 aa00000 7*0 aa00000 7*0
  //   aa00000 7*0 aa00000 7*0 aa00000 7*0 aa00000 7*0 aa00000 7*0 aa00000 7*0 aa00000 7*0 aa00000 7*0
  //   aa00000 7*0 aa00000 7*0 aa00000 7*0 aa00000 7*0 aa00000 7*0 aa00000 7*0 aa00000 7*0 aa00000 7*0
  //   aa00000 7*0 aa00000 7*0 aa00000 7*0 aa00000 7*0 aa00000 7*0 aa00000 7*0 aa00000 7*0 aa00000 7*0
  //   aa00000 7*0 aa00000 7*0 aa00000 7*0 aa00000 7*0 aa00000 7*0 aa00000 7*0 aa00000 7*0 aa00000 7*0
  //   aa00000 7*0 aa00000 7*0 aa00000 7*0 aa00000 7*0 aa00000 7*0 aa00000 7*0 aa00000 7*0 aa00000 7*0
  //   aa00000 7*0 aa00000 7*0 aa00000
endmodule

module bboard (
  input  [3:0] in_1,
  input  in_2,
  input  in_3,
  input  in_4
);

  wire clock_1_out, t_ff_1_q, undriven;
  wire [7:7] pull_resistor_1_node;

  Clock clock_1 (.out(clock_1_out));
  T_Flip_Flop t_ff_1 (.clk(clock_1_out), .Q(t_ff_1_q));  // open: T, Qn, preset, reset
  T_Flip_Flop t_ff_2 (.clk(clock_1_out), .T(t_ff_1_q));  // open: Q, Qn, preset, reset
  Pull_Resistor pull_resistor_1 (.node(pull_resistor_1_node[7]));
  D_Flip_Flop #(.trigger("falling")) d_ff_1 (.preset(undriven));  // open: clk, D, Q, Qn, reset
  D_Flip_Flop #(.trigger("falling")) d_ff_2 (.preset(undriven));  // open: clk, D, Q, Qn, reset
  Register register_1 (.D({{3{pull_resistor_1_node[7]}}, in_2, in_1}), .en(in_3), .clk(in_4));  // open: Q, clr
endmodule

module PC_CIRC (
  input  [15:0] in_1,
  input  in_2,
  input  [2:0] in_3,
  output [15:0] out_4,
  output [15:0] out_5
);

  wire and_1_out, and_2_out, and_3_out, counter_1_carry;

  and and_1 (and_1_out, in_3[1], in_3[0]);
  and and_2 (and_2_out, in_3[0], ~in_3[1]);  // AND_Gate
  Counter counter_1 (
    .load(and_2_out), .D(in_1[7:0]), .count(in_3[1]), .Q(out_5[7:0]), .carry(counter_1_carry),
    .up(and_1_out), .clk(in_2));  // open: clr
  and and_3 (and_3_out, counter_1_carry, in_3[1]);
  Counter counter_2 (
    .load(and_2_out), .D(in_1[15:8]), .count(and_3_out), .Q(out_5[15:8]), .up(and_1_out), .clk(in_2));  // open: carry, clr
  assign out_4 = in_3[2] ? out_5 : 16'bz;  // Controlled_Buffer controlled_buffer_1
endmodule

module SP_CIRC (
  input  [15:0] in_1,
  input  in_2,
  input  [2:0] in_3,
  output [15:0] out_4,
  output [15:0] out_5
);

  wire and_1_out, and_2_out, and_3_out, counter_1_carry;

  and and_1 (and_1_out, in_3[1], in_3[0]);
  and and_2 (and_2_out, in_3[0], ~in_3[1]);  // AND_Gate
  Counter counter_1 (
    .load(and_2_out), .D(in_1[7:0]), .count(in_3[1]), .Q(out_5[7:0]), .carry(counter_1_carry),
    .up(and_1_out), .clk(in_2));  // open: clr
  and and_3 (and_3_out, counter_1_carry, in_3[1]);
  Pull_Resistor pull_resistor_1 (.node(out_5[15:13]));
  Counter #(.max('h1f), .width(5)) counter_2 (
    .load(and_2_out), .D(in_1[12:8]), .count(and_3_out), .Q(out_5[12:8]), .up(and_1_out), .clk(in_2));  // open: carry, clr
  assign out_4 = in_3[2] ? out_5 : 16'bz;  // Controlled_Buffer controlled_buffer_1
endmodule

module MM_CIRC (
  input  [15:0] in_1,
  input  [7:0] in_2,
  input  in_3,
  input  [2:0] in_4,
  output [7:0] out_5,
  output [15:0] out_6,
  output [15:0] out_7
);

  wire decoder_1_out1, decoder_1_out2, decoder_1_out3, decoder_1_out5, decoder_1_out6, decoder_1_out7,
       or_1_out, or_2_out, or_3_out;
  wire [7:0] multiplexer_1_out, multiplexer_2_out;

  Decoder #(.enable("false"), .select(3)) decoder_1 (
    .out1(decoder_1_out1), .out2(decoder_1_out2), .out3(decoder_1_out3), .out5(decoder_1_out5),
    .out6(decoder_1_out6), .out7(decoder_1_out7), .sel(in_4));  // open: out0, out4
  Multiplexer #(.width(8)) multiplexer_1 (.in0(in_2), .in1(in_1[7:0]), .out(multiplexer_1_out), .sel(decoder_1_out1));
  or or_1 (or_1_out, decoder_1_out1, decoder_1_out2);
  or or_2 (or_2_out, decoder_1_out1, decoder_1_out3);
  or or_3 (or_3_out, decoder_1_out6, decoder_1_out7);
  Multiplexer #(.width(8)) multiplexer_2 (.in0(in_2), .in1(in_1[15:8]), .out(multiplexer_2_out), .sel(decoder_1_out1));
  Register register_1 (.D(multiplexer_1_out), .en(or_1_out), .Q(out_7[7:0]), .clk(in_3));  // open: clr
  Multiplexer #(.disabled("Z"), .enable("true"), .width(8)) multiplexer_3 (
    .in0(out_7[7:0]), .in1(out_7[15:8]), .out(out_5), .sel(decoder_1_out7), .en(or_3_out));
  Register register_2 (.D(multiplexer_2_out), .en(or_2_out), .Q(out_7[15:8]), .clk(in_3));  // open: clr
  assign out_6 = decoder_1_out5 ? out_7 : 16'bz;  // Controlled_Buffer controlled_buffer_1
endmodule

module LOG8 (
  input  Clk,
  input  Int,
  input  [7:0] IN8,
  input  HLT,
  output [15:0] OUT16,
  output WE,
  output OE,
  output [7:0] OUT8
);

  wire and_1_out, j_k_ff_1_q, not_1_out, not_2_out, or_1_out, t_ff_1_q, t_ff_2_q;
  wire [2:0] counter_1_q, demultiplexer_1_out0, demultiplexer_1_out1;
  wire [3:0] alu_1_z, pull_resistor_1_node;
  wire [4:0] pla_1_out;
  wire [5:0] pull_resistor_5_node;
  wire [7:0] multiplexer_1_out, multiplexer_3_out, multiplexer_4_out, register_1_q, register_3_q,
       register_4_q, register_5_q, register_6_q, register_7_q, register_8_q;
  wire [9:0] counter_3_q;
  wire [11:11] pull_resistor_2_node;
  wire [15:0] counter_2_q;
  wire [23:8] controlled_buffer_2_out;
  wire [31:0] controlled_buffer_1_out, rom_1_data, rom_2_data;

  not not_1 (not_1_out, HLT);
  Register register_1 (
    .D(multiplexer_1_out), .en(controlled_buffer_1_out[12]), .Q(register_1_q), .clk(Clk));  // open: clr
  Register register_2 (
    .D({pull_resistor_1_node, alu_1_z}), .en(controlled_buffer_1_out[14]), .clk(Clk));  // open: Q, clr
  Pull_Resistor pull_resistor_1 (.node(pull_resistor_1_node));
  J_K_Flip_Flop #(.trigger("falling")) j_k_ff_1 (
    .J(controlled_buffer_1_out[0]), .clk(Clk), .K(and_1_out), .Q(j_k_ff_1_q));  // open: Qn, preset, reset
  and and_1 (and_1_out, j_k_ff_1_q, Int, controlled_buffer_1_out[11], ~t_ff_2_q);  // AND_Gate
  Demultiplexer #(.width(3)) demultiplexer_1 (
    .out0(demultiplexer_1_out0), .out1(demultiplexer_1_out1), .in(counter_1_q), .sel(j_k_ff_1_q));
  Counter #(.max('h7), .ongoal("stay"), .trigger("falling"), .width(3)) counter_1 (
    .count(not_1_out), .Q(counter_1_q), .clk(Clk), .clr(t_ff_1_q));  // open: load, D, carry, up
  T_Flip_Flop #(.trigger("falling")) t_ff_1 (
    .clk(Clk), .T(or_1_out), .Q(t_ff_1_q), .reset(t_ff_1_q));  // open: Qn, preset
  or or_1 (or_1_out, controlled_buffer_1_out[0], controlled_buffer_1_out[11]);
  T_Flip_Flop #(.trigger("falling")) t_ff_2 (
    .clk(Clk), .T(controlled_buffer_1_out[13]), .Q(t_ff_2_q));  // open: Qn, preset, reset
  ROM #(.addrWidth(4), .dataWidth(32)) rom_1 (.addr({Int, demultiplexer_1_out0}), .data(rom_1_data));
  ROM #(.addrWidth(12), .dataWidth(32)) rom_2 (
    .addr({pull_resistor_2_node[11], register_1_q, demultiplexer_1_out1}), .data(rom_2_data));
  Pull_Resistor pull_resistor_2 (.node(pull_resistor_2_node[11]));
  assign {controlled_buffer_1_out[31:3], OE, WE, controlled_buffer_1_out[0]} = not_2_out ? rom_1_data : 32'bz;  // Controlled_Buffer controlled_buffer_1
  not not_2 (not_2_out, j_k_ff_1_q);
  assign {controlled_buffer_1_out[23:16], controlled_buffer_2_out[23:16], OE, WE, controlled_buffer_2_out[13:8], controlled_buffer_1_out[15:8]} = j_k_ff_1_q ? rom_2_data : 32'bz;  // Controlled_Buffer controlled_buffer_2
  Pull_Resistor pull_resistor_3 (.node({controlled_buffer_1_out[23:16], controlled_buffer_2_out[23:16], OE, WE, controlled_buffer_2_out[13:8], controlled_buffer_1_out[15:8]}));
  // Probe on Int
  // Probe on Clk
  // Probe on multiplexer_1_out
  // Probe on OUT16
  PLA #(.in_width(3), .out_width(5), .\table ("001 00111\n010 11001\n100 00010\n101 00100\n110 01000\n111 10000\n000 00000")) pla_1 (
    .in(controlled_buffer_1_out[10:8]), .out(pla_1_out));
  assign OUT16 = controlled_buffer_1_out[7] ? {{13{1'b1}}, controlled_buffer_1_out[6:4]} : 16'bz;  // Controlled_Buffer controlled_buffer_3
  Pull_Resistor pull_resistor_4 (.node({controlled_buffer_1_out[31:3], OE, WE, controlled_buffer_1_out[0]}));
  Multiplexer #(.disabled("Z"), .width(8)) multiplexer_1 (.in1(IN8), .out(multiplexer_1_out), .sel(WE));  // open: in0
  Multiplexer #(.disabled("Z"), .width(8)) multiplexer_2 (.in1(multiplexer_1_out), .out(OUT8), .sel(OE));  // open: in0
  Multiplexer #(.width(8)) multiplexer_3 (
    .in0(multiplexer_1_out), .in1(OUT16[7:0]), .out(multiplexer_3_out), .sel(pla_1_out[0]));
  assign OUT16 = controlled_buffer_1_out[19] ? counter_2_q : 16'bz;  // Controlled_Buffer controlled_buffer_4
  Counter #(.max('hffff), .width(16)) counter_2 (
    .load(controlled_buffer_1_out[17]), .D(OUT16), .count(controlled_buffer_1_out[18]), .Q(counter_2_q),
    .up(controlled_buffer_1_out[16]), .clk(Clk));  // open: carry, clr
  Counter #(.max('h3ff), .width(10)) counter_3 (
    .load(controlled_buffer_1_out[21]), .D(OUT16[9:0]), .count(controlled_buffer_1_out[22]), .Q(counter_3_q),
    .up(controlled_buffer_1_out[20]), .clk(Clk));  // open: carry, clr
  assign OUT16 = controlled_buffer_1_out[23] ? {pull_resistor_5_node, counter_3_q} : 16'bz;  // Controlled_Buffer controlled_buffer_5
  Pull_Resistor pull_resistor_5 (.node(pull_resistor_5_node));
  assign multiplexer_1_out = controlled_buffer_2_out[17] ? register_3_q : 8'bz;  // Controlled_Buffer controlled_buffer_6
  Register register_3 (
    .D(multiplexer_1_out), .en(controlled_buffer_2_out[16]), .Q(register_3_q), .clk(Clk));  // open: clr
  assign multiplexer_1_out = controlled_buffer_2_out[21] ? register_4_q : 8'bz;  // Controlled_Buffer controlled_buffer_7
  Register register_4 (
    .D(multiplexer_1_out), .en(controlled_buffer_2_out[20]), .Q(register_4_q), .clk(Clk));  // open: clr
  ALU alu_1 (
    .A(register_4_q), .B(register_7_q), .cin(controlled_buffer_2_out[13]), .op3(controlled_buffer_2_out[12]),
    .op2(controlled_buffer_2_out[11]), .op1(controlled_buffer_2_out[10]), .op0(controlled_buffer_2_out[9]),
    .X(controlled_buffer_2_out[8]), .O(multiplexer_1_out), .Z(alu_1_z[0]), .G(alu_1_z[1]), .E(alu_1_z[2]),
    .C(alu_1_z[3]));
  Demultiplexer #(.disabled("Z"), .enable("true"), .tristate("true"), .width(8)) demultiplexer_2 (
    .out0(multiplexer_1_out), .out1(OUT16[7:0]), .in(register_5_q), .sel(pla_1_out[0]), .en(pla_1_out[3]));
  Register register_5 (.D(multiplexer_3_out), .en(pla_1_out[1]), .Q(register_5_q), .clk(Clk));  // open: clr
  assign multiplexer_1_out = controlled_buffer_2_out[19] ? register_6_q : 8'bz;  // Controlled_Buffer controlled_buffer_8
  Register register_6 (
    .D(multiplexer_1_out), .en(controlled_buffer_2_out[18]), .Q(register_6_q), .clk(Clk));  // open: clr
  assign multiplexer_1_out = controlled_buffer_2_out[23] ? register_7_q : 8'bz;  // Controlled_Buffer controlled_buffer_9
  Register register_7 (
    .D(multiplexer_1_out), .en(controlled_buffer_2_out[22]), .Q(register_7_q), .clk(Clk));  // open: clr
  Multiplexer #(.width(8)) multiplexer_4 (
    .in0(multiplexer_1_out), .in1(OUT16[15:8]), .out(multiplexer_4_out), .sel(pla_1_out[0]));
  Demultiplexer #(.disabled("Z"), .enable("true"), .tristate("true"), .width(8)) demultiplexer_3 (
    .out0(multiplexer_1_out), .out1(OUT16[15:8]), .in(register_8_q), .sel(pla_1_out[0]), .en(pla_1_out[4]));
  Register register_8 (.D(multiplexer_4_out), .en(pla_1_out[2]), .Q(register_8_q), .clk(Clk));  // open: clr

  // Notes on the sheet:
  //   contents of rom_1 (hex, n*v repeats v):
  //   4004e2 5f2 20201 5*0 80100 c00604 c00704 4c2 5d2 22201
  //   contents of rom_2 (hex, n*v repeats v):
  //   d004010 7*0 d004010 7*0 d004010 7*0 d004010 7*0 d004010 7*0 d004010 7*0 d004010 7*0 d004010 7*0
  //   d004010 8 6*0 d004010 7*0 d004010 7*0 d004010 7*0 d004010 7*0 d004010 7*0 d004010 7*0 d004010 7*0
  //   d004010 d104008 6*0 d004010 7*0 d004010 7*0 d004010 7*0 d004010 7*0 d004010 7*0 d004010 7*0 d004010
  //   7*0 d004010 7*0 d004010 7*0 d004010 7*0 d004010 7*0 d004010 7*0 d004010 7*0 d004010 7*0 d004010 7*0
  //   d004010 7*0 d004010 7*0 d004010 7*0 d004010 7*0 d004010 7*0 d004010 7*0 d004010 7*0 d004010 7*0
  //   d004010 7*0 d004010 7*0 d004010 7*0 d004010 7*0 d004010 7*0 d004010 7*0 d004010 7*0 d004010 7*0
  //   d004010 7*0 d004010 7*0 d004010 7*0 d004010 7*0 d004010 7*0 d004010 7*0 d004010 7*0 d004010 7*0
  //   d004010 7*0 d004010 7*0 d004010 7*0 d004010 7*0 d004010 7*0 d004010 7*0 d004010 7*0 d004010 7*0
  //   d004010 7*0 d004010 7*0 d004010 7*0 d004010 7*0 d004010 7*0 d004010 7*0 d004010 7*0 d004010 7*0
  //   d004010 7*0 d004010 7*0 d004010 7*0 d004010 7*0 d004010 7*0 d004010 7*0 d004010 7*0 d004010 7*0
  //   d004010 7*0 d004010 7*0 d004010 7*0 d004010 7*0 d004010 7*0 d004010 7*0 d004010 7*0 d004010 7*0
  //   d004010 7*0 d004010 7*0 d004010 7*0 d004010 7*0 d004010 7*0 d004010 7*0 d004010 7*0 d004010 7*0
  //   d004010 7*0 d004010 7*0 d004010 7*0 d004010 7*0 d004010 7*0 d004010 7*0 d004010 7*0 d004010 7*0
  //   d004010 7*0 d004010 7*0 d004010 7*0 d004010 7*0 d004010 7*0 d004010 7*0 d004010 7*0 d004010 7*0
  //   d004010 7*0 d004010 7*0 d004010 7*0 d004010 7*0 d004010 7*0 d004010 7*0 d004010 7*0 d004010 7*0
  //   d004010 7*0 d004010 7*0 d004010 7*0 d004010 7*0 d004010 7*0 d004010 7*0 d004010 7*0 d004010 7*0
  //   d004010 7*0 d004010 7*0 d004010 7*0 d004010 7*0 d004010 7*0 d004010 7*0 d004010 7*0 d004010 7*0
  //   d004010 7*0 d004010 7*0 d004010 7*0 d004010 7*0 d004010 7*0 d004010 7*0 d004010 7*0 d004010 7*0
  //   d004010 7*0 d004010 7*0 d004010 7*0 d004010 7*0 d004010 7*0 d004010 7*0 d004010 7*0 d004010 7*0
  //   d004010 7*0 d004010 7*0 d004010 7*0 d004010 7*0 d004010 7*0 d004010 7*0 d004010 7*0 d004010 7*0
  //   d004010 7*0 d004010 7*0 d004010 7*0 d004010 7*0 d004010 7*0 d004010 7*0 d004010 7*0 d004010 7*0
  //   d004010 7*0 d004010 7*0 d004010 7*0 d004010 7*0 d004010 7*0 d004010 7*0 d004010 7*0 d004010 7*0
  //   d004010 7*0 d004010 7*0 d004010 7*0 d004010 7*0 d004010 7*0 d004010 7*0 d004010 7*0 d004010 7*0
  //   d004010 7*0 d004010 7*0 d004010 7*0 d004010 7*0 d004010 7*0 d004010 7*0 d004010 7*0 d004010 7*0
  //   d004010 7*0 d004010 7*0 d004010 7*0 d004010 7*0 d004010 7*0 d004010 7*0 d004010 7*0 d004010 7*0
  //   d004010 7*0 d004010 7*0 d004010 7*0 d004010 7*0 d004010 7*0 d004010 7*0 d004010 7*0 d004010 7*0
  //   d004010 7*0 d004010 7*0 d004010 7*0 d004010 7*0 d004010 7*0 d004010 7*0 d004010 7*0 d004010 7*0
  //   d004010 7*0 d004010 7*0 d004010 7*0 d004010 7*0 d004010 7*0 d004010 7*0 d004010 7*0 d004010 7*0
  //   d004010 7*0 d004010 7*0 d004010 7*0 d004010 7*0 d004010 7*0 d004010 7*0 d004010 7*0 d004010 7*0
  //   d004010 7*0 d004010 7*0 d004010 7*0 d004010 7*0 d004010 7*0 d004010 7*0 d004010 7*0 d004010 7*0
  //   d004010 7*0 d004010 7*0 d004010 7*0 d004010 7*0 d004010 7*0 d004010 7*0 d004010 7*0 d004010 7*0
  //   d004010 7*0 d004010 7*0 d004010 7*0 d004010 7*0 d004010 7*0 d004010 7*0 d004010 7*0 d004010
endmodule
